# Fritzing sketch circuit_diagram (saved by Fritzing 0.8.7b)
circuit board: 19.4861cm x 10.5241cm
stripboards: 4

parts:
  Part1 = Arduino Uno (Rev3)
  U5_-_power_cell_0 = 74HC595 [package="DIP16 [THT]"]
  U6_-_power_cell_1 = 74HC595 [package="DIP16 [THT]"]
  R17 = Resistor [tolerance=±5% resistance=220 package=THT]
  R18 = Resistor [tolerance=±5% resistance=220 package=THT]
  R19 = Resistor [tolerance=±5% resistance=220 package=THT]
  R20 = Resistor [tolerance=±5% resistance=220 package=THT]
  R21 = Resistor [tolerance=±5% resistance=220 package=THT]
  R22 = Resistor [tolerance=±5% resistance=220 package=THT]
  R23 = Resistor [tolerance=±5% resistance=220 package=THT]
  R24 = Resistor [tolerance=±5% resistance=220 package=THT]
  R25 = Resistor [tolerance=±5% resistance=220 package=THT]
  R26 = Resistor [tolerance=±5% resistance=220 package=THT]
  R27 = Resistor [tolerance=±5% resistance=220 package=THT]
  R28 = Resistor [tolerance=±5% resistance=220 package=THT]
  R29 = Resistor [tolerance=±5% resistance=220 package=THT]
  R30 = Resistor [tolerance=±5% resistance=220 package=THT]
  R31 = Resistor [tolerance=±5% resistance=220 package=THT]
  R32 = Resistor [tolerance=±5% resistance=220 package=THT]
  LED_-_power_cell_0 = LED - 5mm [color="Blue (470nm)" package="5 mm [THT]"]
  U7_-_thrower_1 = 74HC595 [package="DIP16 [THT]"]
  R33 = Resistor [tolerance=±5% resistance=220 package=THT]
  U8_-_thrower_0 = 74HC595 [package="DIP16 [THT]"]
  R34 = Resistor [tolerance=±5% resistance=220 package=THT]
  R35 = Resistor [tolerance=±5% resistance=220 package=THT]
  R36 = Resistor [tolerance=±5% resistance=220 package=THT]
  R37 = Resistor [tolerance=±5% resistance=220 package=THT]
  R38 = Resistor [tolerance=±5% resistance=220 package=THT]
  R39 = Resistor [tolerance=±5% resistance=220 package=THT]
  R40 = Resistor [tolerance=±5% resistance=220 package=THT]
  R41 = Resistor [tolerance=±5% resistance=220 package=THT]
  R42 = Resistor [tolerance=±5% resistance=220 package=THT]
  R43 = Resistor [tolerance=±5% resistance=220 package=THT]
  R44 = Resistor [tolerance=±5% resistance=220 package=THT]
  R45 = Resistor [tolerance=±5% resistance=220 package=THT]
  R46 = Resistor [tolerance=±5% resistance=220 package=THT]
  R47 = Resistor [tolerance=±5% resistance=220 package=THT]
  R48 = Resistor [tolerance=±5% resistance=220 package=THT]
  LED_bar_0 = LED_BARGRAPH_10 [package=led_bargaph_10]
  LED_bar_1 = LED_BARGRAPH_10 [package=led_bargaph_10]
  fire_led_1 = LED - 5mm [color="Blue (470nm)" package="5 mm [THT]"]
  fire_led_0 = LED - 5mm [color="Red (633nm)" package="5 mm [THT]"]
  LED_-_power_cell_15 = LED - 5mm [color="Blue (470nm)" package="5 mm [THT]"]
  intensify_but = Momentary Switch [package=ksa_sealed_tac_switch]
  activate_sw = SWITCH-DPDT [package=ayz0202]
  poweron_sw = SWITCH-DPDT [package=ayz0202]

nets:
  N1: Part1.A0, poweron_sw.1
  N2: Part1.A1, intensify_but.4
  N3: Part1.A4/SDA, U7_-_thrower_1.SH_CP, U8_-_thrower_0.SH_CP
  N4: Part1.A5/SCL, U7_-_thrower_1.DS, U8_-_thrower_0.Q7'
  N5: Part1.D8, U5_-_power_cell_0.ST_CP, U6_-_power_cell_1.ST_CP, U7_-_thrower_1.ST_CP, U8_-_thrower_0.ST_CP
  N6: Part1.D6_PWM, U5_-_power_cell_0.SH_CP, U6_-_power_cell_1.SH_CP
  N7: Part1.D7, U5_-_power_cell_0.Q7', U6_-_power_cell_1.DS
  VCC: Part1.5V, U5_-_power_cell_0.VCC, U6_-_power_cell_1.VCC, U7_-_thrower_1.VCC, U8_-_thrower_0.VCC
  GND: Part1.GND, U5_-_power_cell_0.GND, U5_-_power_cell_0.OE, U6_-_power_cell_1.GND, U6_-_power_cell_1.OE, LED_-_power_cell_0.cathode, U7_-_thrower_1.GND, U7_-_thrower_1.OE, R33.Pin_0, U8_-_thrower_0.GND, U8_-_thrower_0.OE, R34.Pin_0, R35.Pin_0, R36.Pin_0, R37.Pin_0, R38.Pin_0, R40.Pin_0, R41.Pin_0, R42.Pin_0, R43.Pin_0, R45.Pin_0, R46.Pin_0, R47.Pin_0, R48.Pin_0, LED_bar_0.A_A, LED_bar_0.B_A, LED_bar_0.C_A, LED_bar_0.D_A, LED_bar_0.E_A, LED_bar_0.F_A, LED_bar_0.G_A, LED_bar_0.H_A, LED_bar_0.I_A, LED_bar_0.J_A, LED_bar_0.J_C, LED_bar_0.I_C, LED_bar_0.H_C, LED_bar_0.G_C, LED_bar_0.F_C, LED_bar_0.E_C, LED_bar_0.D_C, LED_bar_0.C_C, LED_bar_0.B_C, LED_bar_0.A_C, LED_bar_1.A_A, LED_bar_1.B_A, LED_bar_1.C_A, LED_bar_1.D_A, LED_bar_1.E_A, LED_bar_1.F_A, LED_bar_1.G_A, LED_bar_1.H_A, LED_bar_1.I_A, LED_bar_1.J_A, LED_bar_1.J_C, LED_bar_1.I_C, LED_bar_1.H_C, LED_bar_1.G_C, LED_bar_1.F_C, LED_bar_1.E_C, LED_bar_1.D_C, LED_bar_1.C_C, LED_bar_1.B_C, LED_bar_1.A_C, fire_led_1.cathode, fire_led_0.cathode, LED_-_power_cell_15.cathode, activate_sw.2, poweron_sw.2
  N8: U5_-_power_cell_0.Q1, R18.Pin_1
  N9: U5_-_power_cell_0.Q2, R19.Pin_1
  N10: U5_-_power_cell_0.Q3, R20.Pin_1
  N11: U5_-_power_cell_0.Q4, R21.Pin_1
  N12: U5_-_power_cell_0.Q5, R22.Pin_1
  N13: U5_-_power_cell_0.Q6, R23.Pin_1
  N14: U5_-_power_cell_0.Q7, R24.Pin_1
  N15: U5_-_power_cell_0.Q0, R17.Pin_1
  N16: U6_-_power_cell_1.Q1, R26.Pin_1
  N17: U6_-_power_cell_1.Q2, R27.Pin_1
  N18: U6_-_power_cell_1.Q3, R28.Pin_1
  N19: U6_-_power_cell_1.Q4, R29.Pin_1
  N20: U6_-_power_cell_1.Q5, R30.Pin_1
  N21: U6_-_power_cell_1.Q6, R31.Pin_1
  N22: U6_-_power_cell_1.Q7, R32.Pin_1
  N23: U6_-_power_cell_1.Q0, R25.Pin_1
  N24: R17.Pin_0, LED_-_power_cell_0.anode
  N25: R31.Pin_0, LED_-_power_cell_15.anode
  N26: U7_-_thrower_1.Q1, R43.Pin_1
  N27: U7_-_thrower_1.Q2, R42.Pin_1
  N28: U7_-_thrower_1.Q3, R38.Pin_1
  N29: U7_-_thrower_1.Q4, R37.Pin_1
  N30: U7_-_thrower_1.Q5, R41.Pin_1
  N31: U7_-_thrower_1.Q6, R33.Pin_1
  N32: U7_-_thrower_1.Q7, R39.Pin_1
  N33: U7_-_thrower_1.Q0, R48.Pin_1
  N34: U8_-_thrower_0.Q1, R40.Pin_1
  N35: U8_-_thrower_0.Q2, R36.Pin_1
  N36: U8_-_thrower_0.Q3, R46.Pin_1
  N37: U8_-_thrower_0.Q4, R35.Pin_1
  N38: U8_-_thrower_0.Q5, R45.Pin_1
  N39: U8_-_thrower_0.Q6, R34.Pin_1
  N40: U8_-_thrower_0.Q7, R47.Pin_1
  N41: U8_-_thrower_0.Q0, R44.Pin_1
  N42: R39.Pin_0, fire_led_1.anode
  N43: R44.Pin_0, fire_led_0.anode
  N44: intensify_but.2, activate_sw.1

notes:
  Power cell light board (15 LEDs)
  Only 2 LEDs shown for clarity.
  LEDs on every other strip approximately fit power cell window.
  14 elements (2x7 segment)
  Bargraph (fritzing only has 10 segment, ignore extras.)
  Firing LEDs
  In thrower barrel
  Intensify button
  Activate switch
  (I have this wired as safety) Other side of switch lights hat-light on barrel of thrower
  Lower thrower body switch
  (Wired to 'power up')
